# Fritzing sketch Bluetooth RC Car (saved by Fritzing 0.9.3b)

parts:
  Part1 = Arduino Nano (Rev3.0)
  L298N2 = L298N DC motor driver
  BT1 = Bluetooth HC-06u [package=THT]
  M1 = DC Motor  # not connected
  M2 = DC Motor  # not connected
  S1 = Toggle Switch [package=THT]
  7_4V_Li-Ion_Battery_Pack = Lithium Ion Battery Pack 3.7V 4400mAh [part_number=354]

nets:
  N1: Part1.D1/TX, BT1.RXD
  N2: Part1.D0/RX, BT1.TXD
  GND: Part1.GND, BT1.GND
  N3: Part1.D9, L298N2.IN1
  N4: Part1.D10, L298N2.IN2
  N5: Part1.D11/MOSI, L298N2.IN3
  N6: Part1.D12/MISO, L298N2.IN4
  5V: Part1.5V, BT1.VCC
  N7: S1.L1, 7_4V_Li-Ion_Battery_Pack.positive

notes:
  7.4V Li-Ion Battery Pack

custom parts:
  L298N DC motor driver: 2x DC motor driver with 78M05 positive voltage regulator (7..35 V) L298N: max 46 V, 2 A Set 5 V Enable jumper to enable 5 V regultor (needed for the L298N) and +5 V output at screw terminal or supply external +5 V at screw terminal Set ENA and/or ENB to +5 V to enable motor permanently or supply ENA and/or ENB with PWM signal IN1 and IN2 set rotation directory for motor A (OUT1/OUT2) IN2 and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
  Bluetooth HC-06u: Bluetooth HC-06 - face up, pins down 16.5mm x 37.5mm PCB
  Lithium Ion Battery Pack 3.7V 4400mAh: This lithium ion pack is made of 2 balanced 2200mAh cells for a total of 4400mA capacity! The cells are connected in parallel and spot-welded to a protection circuit that provides over-voltage, under-voltage and over-current protection. Each cell can provide 1A of current for about 4 hours so all together the peak current you can draw is a little over 1.5 Amps. Note that these batteries are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
